// Logisim project TESTE.circ as structural Verilog: 3 circuits, main circuit main
module main (
  input  in_1,
  input  in_2,
  input  in_3,
  output out_4,
  output out_5
);

  ADD_1 add_1_1 (.in_1(in_1), .in_2(in_2), .in_3(in_3), .out_4(out_5), .out_5(out_4));
endmodule

module ADD_1 (
  input  in_1,
  input  in_2,
  input  in_3,
  output out_4,
  output out_5
);

  wire and_1_out, and_2_out, and_3_out, and_4_out, and_5_out, and_6_out, and_7_out, not_1_out, not_2_out,
       not_3_out, not_4_out, not_5_out, not_6_out;

  not not_1 (not_1_out, in_1);
  not not_2 (not_2_out, in_2);
  not not_3 (not_3_out, in_1);
  not not_4 (not_4_out, in_3);
  not not_5 (not_5_out, in_2);
  not not_6 (not_6_out, in_3);
  and and_1 (and_1_out, in_2, in_3);
  and and_2 (and_2_out, in_1, in_3);
  and and_3 (and_3_out, in_1, in_2);
  and and_4 (and_4_out, not_1_out, not_2_out, in_3);
  and and_5 (and_5_out, not_3_out, in_2, not_4_out);
  and and_6 (and_6_out, in_1, not_5_out, not_6_out);
  and and_7 (and_7_out, in_1, in_2, in_3);
  or or_1 (out_5, and_1_out, and_2_out, and_3_out);
  ExactlyOne xor_1 (.out(out_4), .in0(and_4_out), .in1(and_5_out), .in2(and_6_out), .in3(and_7_out));
endmodule

module _44 (
  input  in_1,
  input  in_2,
  input  in_3,
  output out_4
);

  // NOT_Gate not_1 has open pins: in=in_1, out=open
  // NOT_Gate not_2 is placed but not wired
  // NOT_Gate not_3 is placed but not wired
  // NOT_Gate not_4 is placed but not wired
  // NOT_Gate not_5 is placed but not wired
  // NOT_Gate not_6 is placed but not wired
  // AND_Gate and_1 is placed but not wired
  // AND_Gate and_2 has open pins: in0=in_1, out=open
  // AND_Gate and_3 is placed but not wired
  // AND_Gate and_4 is placed but not wired
  // AND_Gate and_5 is placed but not wired
  // OR_Gate or_1 is placed but not wired
  // XOR_Gate xor_1 is placed but not wired
endmodule
